# Fritzing sketch Projet SmartPatate BBoard (saved by Fritzing 0.9.3b)
breadboards: 1

parts:
  ArduinoUno = Arduino Uno (Rev3)  # not connected
  C1 = Ceramic Capacitor [capacitance=10nF package="100 mil [THT, multilayer]"]
  D1 = Diode [part_number=1N4548 package=sma-diode_alt]  # not connected
  R2 = Resistor [tolerance=±5% resistance=1M package=THT]  # not connected
  R3 = Resistor [tolerance=±5% resistance=3.3k package=THT]  # not connected
  C2 = Ceramic Capacitor [capacitance=0.1nF package="100 mil [THT, multilayer]"]  # not connected
  R1 = Resistor [tolerance=±5% resistance=10k package=THT]  # not connected

nets:
  Électrode: C1.1
